# Fritzing sketch Circuit Diagram  - Rishav Chakraborty (Home Automation System) (saved by Fritzing 0.9.9b)
breadboards: 1

parts:
  Part1 = Arduino Uno (Rev3)
  Part2 = Bluetooth HC-05 Macho
  U1 = 4-Channel 5v Relay Shield [package=relay-4ch5v10a]
  DHT1 = DHT11 Humitidy and Temperature Sensor
  R1 = Resistor [tolerance=±5% power=0.25 resistance=10k package=THT]
  Part3 = MQ-3 breakout
  Mod2 = KY-012 Active Buzzer Module [package="Breakout board"]
  LED4 = LEDs [package=led10mm]
  LED5 = LEDs [package=led10mm]
  LED6 = smd LED [color="Red (633nm)" package="1206 [SMD]"]
  F1 = Fan - Ventilador [package=THT]
  R2 = Resistor [tolerance=±5% power=0.25 resistance=1 package=THT]
  R3 = Resistor [tolerance=±5% power=0.25 resistance=1 package=THT]
  R4 = Resistor [tolerance=±5% power=0.25 resistance=1 package=THT]
  R5 = Resistor [tolerance=±5% power=0.25 resistance=1 package=THT]
  U2 = LCD-16X2 [package=lcd-16x2]
  R6 = Resistor [tolerance=±5% power=0.25 resistance=220 package=THT]  # not connected
  PS1 = prefix0000 [part_number=S-350-60]
  R7 = Rotary Potentiometer (Small) [maximum_resistance=100kΩ package=THT]
  R8 = Rotary Potentiometer (Small) [maximum_resistance=100kΩ package=THT]

nets:
  N1: Part1.A0, Part3.AO
  N2: Part1.A2, U2.DB4
  N3: Part1.A3, U2.DB5
  N4: Part1.A4/SDA, U2.DB6
  N5: Part1.A5/SCL, U2.DB7
  N6: Part1.D8, Mod2.S
  N7: Part1.D12/MISO, U2.E
  N8: Part1.D13/SCK, U2.RS
  N9: Part1.D0/RX, Part2.TXD
  N10: Part1.D1/TX, Part2.RXD
  N11: Part1.D2, U1.IN4
  N12: Part1.D3_PWM, U1.IN3
  N13: Part1.D4, U1.IN2
  N14: Part1.D5_PWM, U1.IN1
  N15: Part1.D6_PWM, DHT1.DATA, R1.Pin_1
  N16: Part1.D7, Part3.DO
  VCC: Part1.5V, Part2.VCC, U1.VCC, DHT1.VDD, R1.Pin_0, Part3.VCC, U2.VDD, U2.K, R7.leg1
  GND: Part1.GND, Part2.GND, U1.GND, DHT1.GND, Part3.GND, Mod2.-, U2.VSS, U2.R_W, R7.leg2
  N17: U1.K1-In, R2.Pin_1
  N18: U1.K1-On, U1.K2-On, U1.K3-On, U1.K4-On
  N19: U1.K2-In, R3.Pin_1
  N20: U1.K3-In, R4.Pin_1
  N21: U1.K4-In, R5.Pin_1
  N22: LED4.C, LED5.C, LED6.cathode, F1.GND, PS1.connector5, R8.leg2
  N23: LED4.A, R4.Pin_0
  N24: LED5.A, R3.Pin_0
  N25: LED6.anode, R5.Pin_0
  N26: F1.5V, R8.wiper
  N27: R2.Pin_0, R8.leg1
  N28: U2.VO, R7.wiper

notes:
  Switched-Mode Power Supply (SMPS) Unit
  Output: 12V-8.5A, 102W
  16x2 Liquid Crystal Display (LCD)
  (Used in 4-bit Mode)
  DHT11 Digital Temperature and Humidity Sensor
  MQ-3
  Gas Sensor
  HC-05
  Bluetooth Module
  SunFounder 5V Relay
  12V DC Fan
  (Connected to Relay Switch 1)
  12V Warm-White-Light
  Light Emmitting Diode (LED)
  (Connected to Relay Switch 2)
  12V Warm-White-Light
  Light Emmitting Diode (LED)
  (Connected to Relay Switch 3)
  12V Red-Light
  Light Emmitting Diode (LED)
  (Connected to Relay Switch 4)
  Active Buzzer Module
  Arduino UNO R3
  DIY Group Project - Home Automation System.
  Created by Rishav Chakraborty,
  Roll No. 21AG30030, Section 6-A, IIT KGP.

custom parts:
  4-Channel 5v Relay Shield: 4 Channel 5v Relay Shield w. 2x SPD-06VDC-SD-C
  DHT11 Humitidy and Temperature Sensor: DHT11 Humidity and Temperature Sensor
  MQ-3 breakout: Alcohol sensor is capable of detecting alcohol (ethanol) particles on itself and gives the information in digital form back to us to manipulate with it. SKU:101251 • Voltage: 5V DC • Power: max 750mW • Measurement range: 0.04-4mg/L
  KY-012 Active Buzzer Module: Active Piezoelectric Buzzer Module KY-012, it produces single-tone sound when signal is high. (Special thanks to vanepp for fixing the PCB holes and other errors)
  Fan - Ventilador: Ventilador de 2 pines, se encuentra comunmente en computadoras de escritorio
